// Logisim project Matriz leds conecta 4.circ as structural Verilog
module main (
);

  wire _1_out, _2_out, _3_out, _4_out, _5_out, _6_out, clock_1_out, rgbled_27_p1;
  wire [1:0] turno_1_jugador;

  Button _1 (.out(_1_out));
  Turno turno_1 (
    .c1(_1_out), .c2(_2_out), .c3(_3_out), .c4(_4_out), .c5(_5_out), .c6(_6_out), .c7(rgbled_27_p1),
    .Jugador(turno_1_jugador));
  Borde borde_1 ();
  Matriz matriz_1 (
    .Entrada(_1_out), .Clock(clock_1_out), .Jugador(turno_1_jugador));  // open: out_4, out_5, out_6, out_7, out_8, out_9, out_10, out_11, out_12, out_13, out_14, out_15, out_16, out_17, out_18, out_19, out_20, out_21
  // RGBLed #(.multibit("true")) rgbled_1: pin names not known
  // RGBLed #(.multibit("true")) rgbled_2: pin names not known
  // RGBLed #(.multibit("true")) rgbled_3: pin names not known
  // RGBLed #(.multibit("true")) rgbled_4: pin names not known
  // RGBLed #(.multibit("true")) rgbled_5: pin names not known
  // RGBLed #(.multibit("true")) rgbled_6: pin names not known
  Clock clock_1 (.out(clock_1_out));
  Button _3 (.out(_3_out));
  Button _2 (.out(_2_out));
  Borde borde_2 ();
  Borde borde_3 ();
  Matriz matriz_2 (
    .Entrada(_3_out), .Clock(clock_1_out), .Jugador(turno_1_jugador));  // open: out_4, out_5, out_6, out_7, out_8, out_9, out_10, out_11, out_12, out_13, out_14, out_15, out_16, out_17, out_18, out_19, out_20, out_21
  Matriz matriz_3 (
    .Entrada(_4_out), .Clock(clock_1_out), .Jugador(turno_1_jugador));  // open: out_4, out_5, out_6, out_7, out_8, out_9, out_10, out_11, out_12, out_13, out_14, out_15, out_16, out_17, out_18, out_19, out_20, out_21
  Matriz matriz_4 (
    .Entrada(_2_out), .Clock(clock_1_out), .Jugador(turno_1_jugador));  // open: out_4, out_5, out_6, out_7, out_8, out_9, out_10, out_11, out_12, out_13, out_14, out_15, out_16, out_17, out_18, out_19, out_20, out_21
  // RGBLed #(.multibit("true")) rgbled_7: pin names not known
  // RGBLed #(.multibit("true")) rgbled_8: pin names not known
  // RGBLed #(.multibit("true")) rgbled_9: pin names not known
  // RGBLed #(.multibit("true")) rgbled_10: pin names not known
  // RGBLed #(.multibit("true")) rgbled_11: pin names not known
  // RGBLed #(.multibit("true")) rgbled_12: pin names not known
  // RGBLed #(.multibit("true")) rgbled_13: pin names not known
  // RGBLed #(.multibit("true")) rgbled_14: pin names not known
  // RGBLed #(.multibit("true")) rgbled_15: pin names not known
  // RGBLed #(.multibit("true")) rgbled_16: pin names not known
  // RGBLed #(.multibit("true")) rgbled_17: pin names not known
  // RGBLed #(.multibit("true")) rgbled_18: pin names not known
  // RGBLed #(.multibit("true")) rgbled_19: pin names not known
  // RGBLed #(.multibit("true")) rgbled_20: pin names not known
  // RGBLed #(.multibit("true")) rgbled_21: pin names not known
  // RGBLed #(.multibit("true")) rgbled_22: pin names not known
  // RGBLed #(.multibit("true")) rgbled_23: pin names not known
  // RGBLed #(.multibit("true")) rgbled_24: pin names not known
  Button _6 (.out(_6_out));
  Button _4 (.out(_4_out));
  Button _5 (.out(_5_out));
  Borde borde_4 ();
  Borde borde_5 ();
  Borde borde_6 ();
  Matriz matriz_5 (
    .Entrada(_5_out), .Clock(clock_1_out), .Jugador(turno_1_jugador));  // open: out_4, out_5, out_6, out_7, out_8, out_9, out_10, out_11, out_12, out_13, out_14, out_15, out_16, out_17, out_18, out_19, out_20, out_21
  Matriz matriz_6 (
    .Entrada(rgbled_27_p1), .Clock(clock_1_out), .Jugador(turno_1_jugador));  // open: out_4, out_5, out_6, out_7, out_8, out_9, out_10, out_11, out_12, out_13, out_14, out_15, out_16, out_17, out_18, out_19, out_20, out_21
  Matriz matriz_7 (
    .Entrada(_6_out), .Clock(clock_1_out), .Jugador(turno_1_jugador));  // open: out_4, out_5, out_6, out_7, out_8, out_9, out_10, out_11, out_12, out_13, out_14, out_15, out_16, out_17, out_18, out_19, out_20, out_21
  // RGBLed #(.multibit("true")) rgbled_25: pin names not known
  // RGBLed #(.multibit("true")) rgbled_26: pin names not known
  // RGBLed #(.multibit("true")) rgbled_27: pin names not known; wires that end beside it: rgbled_27_p1
  // RGBLed #(.multibit("true")) rgbled_28: pin names not known
  // RGBLed #(.multibit("true")) rgbled_29: pin names not known
  // RGBLed #(.multibit("true")) rgbled_30: pin names not known
  // RGBLed #(.multibit("true")) rgbled_31: pin names not known
  // RGBLed #(.multibit("true")) rgbled_32: pin names not known
  // RGBLed #(.multibit("true")) rgbled_33: pin names not known
  // RGBLed #(.multibit("true")) rgbled_34: pin names not known
  // RGBLed #(.multibit("true")) rgbled_35: pin names not known
  // RGBLed #(.multibit("true")) rgbled_36: pin names not known
  // RGBLed #(.multibit("true")) rgbled_37: pin names not known
  // RGBLed #(.multibit("true")) rgbled_38: pin names not known
  // RGBLed #(.multibit("true")) rgbled_39: pin names not known
  // RGBLed #(.multibit("true")) rgbled_40: pin names not known
  // RGBLed #(.multibit("true")) rgbled_41: pin names not known
  // RGBLed #(.multibit("true")) rgbled_42: pin names not known
  Button _7 (.out(rgbled_27_p1));
  Borde borde_7 ();
  Borde borde_8 ();
endmodule

module Turno (
  input  c1,
  input  c2,
  input  c3,
  input  c4,
  input  c5,
  input  c6,
  input  c7,
  output [1:0] Jugador
);

  wire counter_1_carry, or_1_out;

  Counter #(.width(2), .max('h2)) counter_1 (
    .load(counter_1_carry), .D(2'b01), .Q(Jugador), .carry(counter_1_carry), .clk(or_1_out));  // open: count, clr, preset, down
  or or_1 (or_1_out, c1, c2, c3, c4, c5, c6, c7);
endmodule

module Matriz (
  input  Entrada,
  input  Clock,
  input  [1:0] Jugador,
  output [7:0] out_4,
  output [7:0] out_5,
  output [7:0] out_6,
  output [7:0] out_7,
  output [7:0] out_8,
  output [7:0] out_9,
  output [7:0] out_10,
  output [7:0] out_11,
  output [7:0] out_12,
  output [7:0] out_13,
  output [7:0] out_14,
  output [7:0] out_15,
  output [7:0] out_16,
  output [7:0] out_17,
  output [7:0] out_18,
  output [7:0] out_19,
  output [7:0] out_20,
  output [7:0] out_21
);

  wire and_2_out, comparator_1_lt, counter_1_carry, counter_1_q, counter_2_carry, demultiplexer_1_out0,
       demultiplexer_1_out1, demultiplexer_1_out2, demultiplexer_1_out3, demultiplexer_1_out4,
       demultiplexer_1_out5, not_1_out, On;
  wire [0:0] and_1_out;
  wire [1:0] _1_q, _2_q, _3_q, _4_q, _5_q, _6_q, demultiplexer_2_out0, demultiplexer_2_out1,
       demultiplexer_2_out2, demultiplexer_2_out3, demultiplexer_2_out4, demultiplexer_2_out5;
  wire [2:0] ocupados, posix;

  Demultiplexer #(.select(3), .enable("false")) demultiplexer_1 (
    .out0(demultiplexer_1_out0), .out1(demultiplexer_1_out1), .out2(demultiplexer_1_out2),
    .out3(demultiplexer_1_out3), .out4(demultiplexer_1_out4), .out5(demultiplexer_1_out5), .in(On),
    .sel(posix));  // open: out6, out7
  Demultiplexer #(.select(3), .width(2), .enable("false")) demultiplexer_2 (
    .out0(demultiplexer_2_out0), .out1(demultiplexer_2_out1), .out2(demultiplexer_2_out2),
    .out3(demultiplexer_2_out3), .out4(demultiplexer_2_out4), .out5(demultiplexer_2_out5), .in(Jugador),
    .sel(posix));  // open: out6, out7
  Register #(.width(2), .Select("low")) _1 (
    .D(demultiplexer_2_out0), .Q(_1_q), .clk(demultiplexer_1_out0));  // open: en, clr
  Color color_1 (.Jugador(_1_q), .out_2({out_4, out_5, out_6}));
  Register #(.width(2), .trigger("high"), .Select("low")) _2 (
    .D(demultiplexer_2_out1), .Q(_2_q), .clk(demultiplexer_1_out1));  // open: en, clr
  Color color_2 (.Jugador(_2_q), .out_2({out_7, out_8, out_9}));
  Register #(.width(2), .trigger("high"), .Select("low")) _3 (
    .D(demultiplexer_2_out2), .Q(_3_q), .clk(demultiplexer_1_out2));  // open: en, clr
  Color color_3 (.Jugador(_3_q), .out_2({out_10, out_11, out_12}));
  Register #(.width(2), .trigger("high"), .Select("low")) _4 (
    .D(demultiplexer_2_out3), .Q(_4_q), .clk(demultiplexer_1_out3));  // open: en, clr
  Color color_4 (.Jugador(_4_q), .out_2({out_13, out_14, out_15}));
  Register #(.width(2), .trigger("high"), .Select("low")) _5 (
    .D(demultiplexer_2_out4), .Q(_5_q), .clk(demultiplexer_1_out4));  // open: en, clr
  Color color_5 (.Jugador(_5_q), .out_2({out_16, out_17, out_18}));
  Register #(.width(2), .trigger("high"), .Select("low")) _6 (
    .D(demultiplexer_2_out5), .Q(_6_q), .clk(demultiplexer_1_out5));  // open: en, clr
  Color color_6 (.Jugador(_6_q), .out_2({out_19, out_20, out_21}));
  Subtractor #(.width(3)) subtractor_1 (.a(3'b101), .b(ocupados), .out(posix));  // open: bin, bout
  Comparator #(.width(3), .mode("unsigned")) comparator_1 (
    .a(ocupados), .b(3'b110), .lt(comparator_1_lt));  // open: gt, eq
  and and_1 (and_1_out[0], comparator_1_lt, counter_1_q);
  Counter #(.width(1), .max('h1), .ongoal("continue"), .trigger("falling")) counter_1 (
    .D(Entrada), .Q(counter_1_q), .carry(counter_1_carry), .clk(Entrada), .clr(and_2_out));  // open: load, count, preset, down
  and and_2 (and_2_out, Clock, counter_1_carry);
  and and_3 (On, Clock, and_1_out[0]);
  Counter #(.width(3), .max('h6), .trigger("falling")) counter_2 (
    .D({2'b00, and_1_out[0]}), .count(not_1_out), .Q(ocupados), .carry(counter_2_carry), .clk(On));  // open: load, clr, preset, down
  not not_1 (not_1_out, counter_2_carry);
endmodule

module Color (
  input  [1:0] Jugador,
  output [23:0] out_2
);

  // RGBLed #(.multibit("true")) rgbled_1: pin names not known
  Multiplexer #(.select(2), .width(24), .enable("false")) multiplexer_1 (
    .in0(24'h808080), .in1(24'h6a0dad), .in2(24'hff00), .out(out_2), .sel(Jugador));  // open: in3
endmodule
